# Fritzing sketch Nwm (saved by Fritzing 0.9.3b)
breadboards: 1

parts:
  Power_plug1 = Power plug
  R1 = Resistor [tolerance=±5% resistance=2.2k package=THT]
  DI1 = 7-Segment LED Display [package=THT]

nets:
  N1: Power_plug1.GND, DI1.cathodeDP
  N2: Power_plug1.VCC, R1.Pin_0
  N3: R1.Pin_1, DI1.commAnode
