# Fritzing sketch R1_pomiar_oporu (saved by Fritzing 0.9.3b)
breadboards: 1

parts:
  R1 = Resistor [tolerance=±5% resistance=220 package=THT]  # not connected
  R2 = Resistor [tolerance=±5% resistance=1k package=THT]
  R3 = Resistor [tolerance=±5% resistance=2.2k package=THT]
  R4 = Resistor [tolerance=±5% resistance=1k package=THT]
  R5 = Resistor [tolerance=±5% resistance=220 package=THT]

nets:
  N1: R2.Pin_0, R3.Pin_0, R4.Pin_1
  N2: R2.Pin_1, R3.Pin_1, R5.Pin_0
  N3: R4.Pin_0, R5.Pin_1
