# Fritzing sketch a (saved by Fritzing 0.9.3b)
breadboards: 1

parts:
  R3 = Resistor [tolerance=±5% resistance=1k package=THT]
  R1 = Resistor [tolerance=±5% resistance=2.2k package="2512 [SMD]"]
  R2 = Resistor [tolerance=±10% resistance=2.2k package="0402 [SMD]"]

nets:
  N1: R3.Pin_0, R1.Pin_0
  N2: R3.Pin_1, R2.Pin_1
  N3: R1.Pin_1, R2.Pin_0
