# Fritzing sketch d (saved by Fritzing 0.9.3b)
breadboards: 1

parts:
  R1 = Resistor [tolerance=±5% resistance=1k package=THT]
  R2 = Resistor [tolerance=±10% resistance=2.2k package=THT]
  R3 = Resistor [tolerance=±5% resistance=100 package=THT]
  R4 = Resistor [tolerance=±5% resistance=2.2k package=THT]
  R5 = Resistor [tolerance=±5% resistance=1k package=THT]

nets:
  N1: R1.Pin_0, R3.Pin_1
  N2: R1.Pin_1, R2.Pin_0, R4.Pin_0
  N3: R2.Pin_1, R3.Pin_0, R5.Pin_1
  N4: R4.Pin_1, R5.Pin_0
